# Fritzing sketch SNES2JoystickPort (saved by Fritzing 0.9.1b)
circuit board: 7.01621cm x 3.04548cm
breadboards: 1

parts:
  XTAL1 = Crystal [frequency="16 Mhz" package=THT]
  X1 = DB9 Connector [package=db9]
  U1 = atmega328 [package=dip]
  C1 = Capacitor [package=cap-pth-small2]
  C2 = Capacitor [package=cap-pth-small2]
  R1 = Resistor [tolerance=±5% resistance=10k package=THT]
  J1 = shrouded pin header, 10 pins [form="♂ (shrouded male)"]

nets:
  N1: XTAL1.pin_0, U1.XLAT2, C1.2
  N2: XTAL1.pin_1, U1.XLAT1, C2.2
  N3: X1.2, U1.D12
  N4: X1.3, U1.D11_(PWM)
  N5: X1.4, U1.D10_(PWM)
  N6: X1.5, U1.D9_(PWM)
  N7: X1.7, U1.GND, C1.1, C2.1, J1.pin6
  N8: X1.8, U1.VCC, U1.AVCC, R1.Pin_1, J1.pin5
  N9: X1.9, U1.D13
  N10: U1.RESET, R1.Pin_0
  N11: U1.D2, J1.pin3
  N12: U1.D3_(PWM), J1.pin2
  N13: U1.D4, J1.pin1
